# Fritzing sketch HC-05-Bluetooth (saved by Fritzing 0.9.3b)

parts:
  Componente1 = Arduino Mega 2560 (Rev3)
  BAT1 = BC9VPC [package=bc9vpc]
  Componente4 = Bluetooth HC-05 Macho
  Componente6 = Logic Level Converter

nets:
  N1: Componente1.D12_PWM, Componente6.TX_HV
  N2: Componente1.D11_PWM, Componente6.TX2_HV
  N3: Componente1.D10_PWM, Componente6.RX_HV
  N4: Componente1.3V3, Componente4.Key, Componente6.LV
  5V: Componente1.5V, Componente4.VCC, Componente6.HV
  GND: Componente1.GND, BAT1.V-, Componente4.GND, Componente6.GND
  N5: Componente1.VIN, BAT1.V+
  N6: Componente4.State, Componente6.TX_LV
  N7: Componente4.TXD, Componente6.TX2_LV
  N8: Componente4.RXD, Componente6.RX_LV

notes:
  Key - ON BEFORE START TO ENTER AT Mode
