# Fritzing sketch MPU-9250 (saved by Fritzing 0.9.3b)

parts:
  Componente1 = Arduino Mega 2560 (Rev3)
  BAT1 = BC9VPC [package=bc9vpc]
  Componente2 = MPU-9250/6500

nets:
  N1: Componente1.D21/SCL, Componente2.SCL
  N2: Componente1.D20/SDA, Componente2.SDA
  3V3: Componente1.3V3, Componente2.VCC
  GND: Componente1.GND, BAT1.V-, Componente2.GND
  N3: Componente1.VIN, BAT1.V+
