# Fritzing sketch motors (saved by Fritzing 0.9.3b)
breadboards: 1

parts:
  Componente1 = Arduino Mega 2560 (Rev3)
  Componente2 = Motor Driver 1A Dual TB6612FNG  # not connected
  Componente3 = Motor Driver 1A Dual TB6612FNG
  BAT1 = BC9VPC [package=bc9vpc]
  BAT2 = BC9VPC [package=bc9vpc]
  M1 = DC Motor
  M2 = DC Motor
  M4 = DC Motor
  M3 = DC Motor
  D1 = Rectifier Diode [part_number=1N4001 package="300 mil [THT]"]
  D2 = Rectifier Diode [part_number=1N4001 package="300 mil [THT]"]
  D3 = Rectifier Diode [part_number=1N4001 package="300 mil [THT]"]
  D4 = Rectifier Diode [part_number=1N4001 package="300 mil [THT]"]
  D5 = Rectifier Diode [part_number=1N4001 package="300 mil [THT]"]
  D6 = Rectifier Diode [part_number=1N4001 package="300 mil [THT]"]
  D7 = Rectifier Diode [part_number=1N4001 package="300 mil [THT]"]
  D8 = Rectifier Diode [part_number=1N4001 package="300 mil [THT]"]
  D9 = Rectifier Diode [part_number=1N4001 package="300 mil [THT]"]
  D10 = Rectifier Diode [part_number=1N4001 package="300 mil [THT]"]
  D11 = Rectifier Diode [part_number=1N4001 package="300 mil [THT]"]
  D12 = Rectifier Diode [part_number=1N4001 package="300 mil [THT]"]
  D13 = Rectifier Diode [part_number=1N4001 package="300 mil [THT]"]
  D14 = Rectifier Diode [part_number=1N4001 package="300 mil [THT]"]
  D15 = Rectifier Diode [part_number=1N4001 package="300 mil [THT]"]
  D16 = Rectifier Diode [part_number=1N4001 package="300 mil [THT]"]

nets:
  N1: Componente1.GND, BAT1.V-, BAT2.V-, D1.anode, D3.anode, D7.anode, D8.anode, D9.anode, D10.anode, D11.anode, D12.anode
  N2: Componente1.VIN, BAT1.V+
  N3: Componente3.A02, M1.pin_1, D5.anode, D7.cathode
  N4: Componente3.A01, M1.pin_2, D6.anode, D8.cathode
  N5: BAT2.V+, D2.cathode, D4.cathode, D5.cathode, D6.cathode, D13.cathode, D14.cathode, D15.cathode, D16.cathode
  N6: M2.pin_1, D9.cathode, D15.anode
  N7: M2.pin_2, D10.cathode, D13.anode
  N8: M4.pin_1, D11.cathode, D14.anode
  N9: M4.pin_2, D12.cathode, D16.anode
  N10: M3.pin_1, D3.cathode, D4.anode
  N11: M3.pin_2, D1.cathode, D2.anode

notes:
  Front
  back
