# Fritzing sketch photoelectric_encoder (saved by Fritzing 0.9.3b)
breadboards: 1

parts:
  Componente1 = Arduino Mega 2560 (Rev3)
  BAT1 = BC9VPC [package=bc9vpc]
  U1 = CNZ1120 [package=cnz1120]
  U2 = CNZ1120 [package=cnz1120]
  U3 = CNZ1120 [package=cnz1120]
  U4 = CNZ1120 [package=cnz1120]

nets:
  N1: Componente1.D19/RX1, U4.3
  N2: Componente1.D18/TX1, U2.3
  N3: Componente1.5V, U1.2, U2.2, U3.2, U4.2
  N4: Componente1.GND, BAT1.V-, U1.1, U2.1, U3.1, U4.1
  N5: Componente1.VIN, BAT1.V+
  N6: Componente1.D2_PWM, U1.3
  N7: Componente1.D3_PWM, U3.3
  N8: Componente1.D35, U1.4
  N9: Componente1.D36, U3.4
  N10: Componente1.D37, U2.4
  N11: Componente1.D38, U4.4

notes:
  Front
  back
