# Fritzing sketch us_array (saved by Fritzing 0.9.3b)

parts:
  Componente1 = Arduino Mega 2560 (Rev3)
  BAT1 = BC9VPC [package=bc9vpc]
  hc-sr1 = hc-sr04
  hc-sr2 = hc-sr04
  hc-sr3 = hc-sr04
  hc-sr4 = hc-sr04
  hc-sr5 = hc-sr04
  hc-sr6 = hc-sr04
  hc-sr7 = hc-sr04
  hc-sr8 = hc-sr04
  hc-sr9 = hc-sr04
  hc-sr10 = hc-sr04
  hc-sr11 = hc-sr04
  hc-sr12 = hc-sr04

nets:
  VCC: Componente1.5V, hc-sr1.VCC, hc-sr2.VCC, hc-sr3.VCC, hc-sr4.VCC, hc-sr5.VCC, hc-sr6.VCC, hc-sr7.VCC, hc-sr8.VCC, hc-sr9.VCC, hc-sr10.VCC, hc-sr11.VCC, hc-sr12.VCC
  GND: Componente1.GND, BAT1.V-, hc-sr1.GND, hc-sr2.GND, hc-sr3.GND, hc-sr4.GND, hc-sr5.GND, hc-sr6.GND, hc-sr7.GND, hc-sr8.GND, hc-sr9.GND, hc-sr10.GND, hc-sr11.GND, hc-sr12.GND
  N1: Componente1.VIN, BAT1.V+
  N2: Componente1.D23, hc-sr6.Trig, hc-sr6.Echo
  N3: Componente1.D24, hc-sr7.Trig, hc-sr7.Echo
  N4: Componente1.D25, hc-sr8.Trig, hc-sr8.Echo
  N5: Componente1.D26, hc-sr1.Trig, hc-sr1.Echo
  N6: Componente1.D27, hc-sr10.Trig, hc-sr10.Echo
  N7: Componente1.D28, hc-sr12.Trig, hc-sr12.Echo
  N8: Componente1.D29, hc-sr11.Trig, hc-sr11.Echo
  N9: Componente1.D30, hc-sr5.Trig, hc-sr5.Echo
  N10: Componente1.D31, hc-sr2.Trig, hc-sr2.Echo
  N11: Componente1.D32, hc-sr9.Trig, hc-sr9.Echo
  N12: Componente1.D33, hc-sr4.Trig, hc-sr4.Echo
  N13: Componente1.D34, hc-sr3.Trig, hc-sr3.Echo

notes:
  Front <- clockwise order
  000 º
  030 º
  060 º
  090 º
  120 º
  150 º
  180 º
  210 º
  240 º
  270 º
  300 º
  330 º
